// Logisim project SAP mod.circ as structural Verilog: 21 circuits, main circuit main
module main (
  input  Reset,
  output [3:0] \Endereço ,
  output [3:0] Dados,
  output out_4,
  output out_5,
  output out_6,
  output out_7,
  output out_8,
  output out_9,
  output out_10,
  output out_11
);

  wire CLK, Clock_out, comparador_1_out_4, comparador_1_out_5, controlador_sequencializador_1_hlt, Cp, Dec,
       Ea, Ec, Ep, Eu, nCE, nEi, nLa, nLb, nLi, nLm, nLo, not_1_out, not_2_out, not_3_out, not_4_out,
       \registrador_instruções_1_i4 , \registrador_instruções_1_i5 , \registrador_instruções_1_i6 ,
       \registrador_instruções_1_i7 , Su;
  wire [3:0] rem_1_remout;
  wire [7:0] acumulador_1_a_out_ula, registrador_b_1_b_dataout;

  Clock Clock (.out(Clock_out));
  not not_1 (not_1_out, CLK);
  not not_2 (not_2_out, Reset);
  not not_3 (not_3_out, nCE);
  assign CLK = not_4_out ? Clock_out : 1'bz;  // Controlled_Buffer controlled_buffer_1
  not not_4 (not_4_out, controlador_sequencializador_1_hlt);
  REM rem_1 (.in_1(Dados), .nLm(nLm), .CLK(CLK), .REMOut(rem_1_remout));
  Contador_Programa contador_programa_1 (.Cp(Cp), .nCLK(not_1_out), .nCLR(not_2_out), .Ep(Ep), .Cp_Out(Dados));
  \Memória_RAM  \memória_ram_1  (.in_1(rem_1_remout), .nCE(not_3_out), .CLK(CLK), .out_4({\Endereço , Dados}));
  \Registrador_Instruções  \registrador_instruções_1  (
    .in_1({\Endereço , Dados}), .nLi(nLi), .CLK(CLK), .CLR(Reset), .nEi(nEi), .out_6({\Endereço , Dados}),
    .I4(\registrador_instruções_1_i4 ), .I5(\registrador_instruções_1_i5 ),
    .I6(\registrador_instruções_1_i6 ), .I7(\registrador_instruções_1_i7 ));
  Controlador_Sequencializador controlador_sequencializador_1 (
    .CLR(Reset), .I7(\registrador_instruções_1_i7 ), .Ep(Ep), .Cp(Cp), .I6(\registrador_instruções_1_i6 ),
    .I5(\registrador_instruções_1_i5 ), .I4(\registrador_instruções_1_i4 ),
    .HLT(controlador_sequencializador_1_hlt), .nLm(nLm), .nCE(nCE), .nEl(nEi), .nLa(nLa), .Ea(Ea), .Su(Su),
    .Eu(Eu), .nLb(nLb), .nLo(nLo), .nLl(nLi), .CLK(CLK), .Ec(Ec), .DEC(Dec));
  Acumulador acumulador_1 (
    .A_In({\Endereço , Dados}), .nLa(nLa), .CLK(CLK), .Ea(Ea), .A_Out_ULA(acumulador_1_a_out_ula),
    .A_Out({\Endereço , Dados}));
  Somador_Subtrator somador_subtrator_1 (
    .Su(Dec), .B_data(registrador_b_1_b_dataout), .A_dataOut2({\Endereço , Dados}),
    .A_data(acumulador_1_a_out_ula), .Eu(Eu), .DEC(Su));
  Registrador_B registrador_b_1 (
    .B_dataIn({\Endereço , Dados}), .B_dataOut(registrador_b_1_b_dataout), .nLb(nLb), .CLK(CLK));
  Hex_Digit_Display hex_digit_display_1 (.value({out_4, out_5, out_6, out_7}));  // open: dp
  \Indicação_Visual  \indicação_visual_1  (
    .Input({\Endereço , Dados}), .Output({out_4, out_5, out_6, out_7, out_8, out_9, out_10, out_11}),
    .nLo(nLo), .CLK(CLK), .CLR(Reset));
  Comparador comparador_1 (
    .B_data(registrador_b_1_b_dataout), .A_data(acumulador_1_a_out_ula), .in_1(Ec),
    .out_4(comparador_1_out_4), .out_5(comparador_1_out_5));
  DotMatrix #(.matrixcols(8), .matrixrows(1), .dotshape("circle")) dotmatrix_1 (
    .col0(out_4), .col1(out_5), .col2(out_6), .col3(out_7), .col4(out_8), .col5(out_9), .col6(out_10),
    .col7(out_11));
  Hex_Digit_Display hex_digit_display_2 (.value({out_8, out_9, out_10, out_11}));  // open: dp
  _7_Segment_Display u_7_segment_display_1 (.g(comparador_1_out_5));  // open: f, a, b, e, d, c, dp
  _7_Segment_Display u_7_segment_display_2 (
    .f(comparador_1_out_4), .a(comparador_1_out_4), .b(1'b1), .e(comparador_1_out_4), .d(comparador_1_out_4),
    .c(1'b1));  // open: g, dp

  // Other names for the same wires on the sheet: CLR = Reset

  // Notes on the sheet:
  //   Instruções:
  //   - 0000: pegar o valor
  //   - 0001: somar o valor
  //   - 0010: subtrair o valor
  //   - 0011: decrementa o valor no acumulador em um.
  //   - 0100: compara dois valores
  //   - 1111: interromper o circuito
  //   - 1110: exibir o valor
  //   Operações:
  //   - 09 e0 2a e0 1b e0 2c e0 f0 08 06 07 05 00 00 00
  //   - 08 - 06 + 07 - 05 = 04
endmodule

module Contador_Programa (
  input  Cp,
  input  nCLK,
  input  nCLR,
  input  Ep,
  output [3:0] Cp_Out
);

  wire not_1_out;
  wire [3:0] counter_1_q;

  not not_1 (not_1_out, nCLR);
  Counter #(.width(4), .max('hf), .trigger("falling")) counter_1 (
    .count(Cp), .Q(counter_1_q), .clk(nCLK), .clr(not_1_out));  // open: load, D, carry
  assign Cp_Out = Ep ? counter_1_q : 4'bz;  // Controlled_Buffer controlled_buffer_1
endmodule

module REM (
  input  [3:0] in_1,
  input  nLm,
  input  CLK,
  output [3:0] REMOut
);

  wire not_1_out;

  not not_1 (not_1_out, nLm);
  Register #(.width(4)) register_1 (.D(in_1), .en(not_1_out), .Q(REMOut), .clk(CLK));  // open: clr
endmodule

module \Memória_RAM  (
  input  [3:0] in_1,
  input  nCE,
  input  CLK,
  output [7:0] out_4
);

  RAM #(.addrWidth(4)) ram_1 (.addr(in_1), .data(out_4), .sel(nCE), .clk(CLK), .ld(nCE));  // open: clr

  // Notes on the sheet:
  //   Operações:
  //   - 09 e0 2a e0 1b e0 2c e0 f0 08 06 07 05 00 00 00
  //   - 08 - 06 + 07 - 05 = 04
endmodule

module \Registrador_Instruções  (
  input  [7:0] in_1,
  input  nLi,
  input  CLK,
  input  CLR,
  input  nEi,
  output [7:0] out_6,
  output I4,
  output I5,
  output I6,
  output I7
);

  wire not_1_out, not_2_out;
  wire [3:0] register_1_q;
  wire [7:0] bit_extender_1_out;

  not not_1 (not_1_out, nLi);
  not not_2 (not_2_out, nEi);
  Register register_1 (.D(in_1), .en(not_1_out), .Q({I7, I6, I5, I4, register_1_q}), .clk(CLK), .clr(CLR));
  assign bit_extender_1_out = {{4{1'b0}}, register_1_q};  // Bit_Extender bit_extender_1
  assign out_6 = not_2_out ? bit_extender_1_out : 8'bz;  // Controlled_Buffer controlled_buffer_1
endmodule

module Acumulador (
  input  [7:0] A_In,
  input  nLa,
  input  CLK,
  input  Ea,
  output [7:0] A_Out_ULA,
  output [7:0] A_Out
);

  wire not_1_out;

  not not_1 (not_1_out, nLa);
  Register register_1 (.D(A_In), .en(not_1_out), .Q(A_Out_ULA), .clk(CLK));  // open: clr
  assign A_Out = Ea ? A_Out_ULA : 8'bz;  // Controlled_Buffer controlled_buffer_1
endmodule

module Somador_Subtrator (
  input  Su,
  input  DEC,
  input  [7:0] B_data,
  input  [7:0] A_data,
  input  Eu,
  output [7:0] A_dataOut2
);

  wire not_1_out;
  wire [7:0] adder_1_out, bit_extender_1_out, controlled_buffer_1_out, xor_1_out;

  assign bit_extender_1_out = {{7{1'b0}}, DEC};  // Bit_Extender bit_extender_1
  assign controlled_buffer_1_out = DEC ? bit_extender_1_out : 8'bz;  // Controlled_Buffer controlled_buffer_1
  not not_1 (not_1_out, DEC);
  assign controlled_buffer_1_out = not_1_out ? B_data : 8'bz;  // Controlled_Buffer controlled_buffer_2
  assign xor_1_out = {8{Su}} ^ controlled_buffer_1_out;  // XOR_Gate xor_1, 8 bits wide
  Adder adder_1 (.a(xor_1_out), .b(A_data), .out(adder_1_out), .cin(Su));  // open: cout
  assign A_dataOut2 = Eu ? adder_1_out : 8'bz;  // Controlled_Buffer controlled_buffer_3
endmodule

module Registrador_B (
  input  [7:0] B_dataIn,
  input  nLb,
  input  CLK,
  output [7:0] B_dataOut
);

  wire not_1_out;

  Register register_1 (.D(B_dataIn), .en(not_1_out), .Q(B_dataOut), .clk(CLK));  // open: clr
  not not_1 (not_1_out, nLb);
endmodule

module Controlador_Sequencializador (
  input  CLK,
  input  CLR,
  input  I7,
  input  I6,
  input  I5,
  input  I4,
  output Ep,
  output Cp,
  output DEC,
  output HLT,
  output nLm,
  output nCE,
  output nEl,
  output nLa,
  output Ea,
  output Su,
  output Eu,
  output nLb,
  output nLo,
  output nLl,
  output Ec
);

  wire c39_1_out_8, c39_1_out_9, c39_1_out_10, c39_1_out_11, c40_1_out_8, c40_1_out_9, c40_1_out_10,
       c40_1_out_11, c41_1_out_9, c41_1_out_10, c41_1_out_11, c41_1_out_12, c41_2_out_11, c41_2_out_12,
       c43_1_out_7, c43_1_out_8, c43_1_out_9, c44_1_out_9, c44_1_out_10, c45_1_out_7, c45_1_out_8,
       c46_1_out_6, c47_1_out_3, controlled_buffer_1_out, decodificador_1_add, decodificador_1_cmp,
       decodificador_1_dec, decodificador_1_lda, decodificador_1_out, decodificador_1_sub, nor_1_out,
       not_1_out, not_2_out, shift_register_1_q2, shift_register_1_q3, shift_register_1_q4,
       shift_register_1_q5;

  Decodificador decodificador_1 (
    .LDA(decodificador_1_lda), .ADD(decodificador_1_add), .SUB(decodificador_1_sub),
    .OUT(decodificador_1_out), .HLT(HLT), .l7(I7), .l6(I6), .l5(I5), .l4(I4), .CMP(decodificador_1_cmp),
    .DEC(decodificador_1_dec));
  not not_1 (not_1_out, decodificador_1_dec);
  C48 c48_1 (.in_1(shift_register_1_q5), .in_2(decodificador_1_dec), .out_3(DEC));
  assign controlled_buffer_1_out = not_1_out ? decodificador_1_sub : 1'bz;  // Controlled_Buffer controlled_buffer_1
  assign controlled_buffer_1_out = decodificador_1_dec ? decodificador_1_dec : 1'bz;  // Controlled_Buffer controlled_buffer_2
  C39 c39_1 (
    ._1(decodificador_1_lda), ._4(decodificador_1_add), ._9(controlled_buffer_1_out),
    ._10(shift_register_1_q3), ._12(decodificador_1_lda), ._13(shift_register_1_q4), .out_8(c39_1_out_8),
    .out_9(c39_1_out_9), .out_10(c39_1_out_10), .out_11(c39_1_out_11), .in_1(decodificador_1_cmp));
  not not_2 (not_2_out, CLK);
  C40 c40_1 (
    ._1(decodificador_1_add), .SUB(controlled_buffer_1_out), ._5(shift_register_1_q4),
    ._9(decodificador_1_lda), ._12(decodificador_1_add), ._13(shift_register_1_q3), .out_8(c40_1_out_8),
    .out_9(c40_1_out_9), .out_10(c40_1_out_10), .out_11(c40_1_out_11), .CMP(decodificador_1_cmp));
  C44 c44_1 (
    .in_1(Ep), .in_2(c39_1_out_8), .in_3(c39_1_out_9), .in_4(c39_1_out_10), .in_5(shift_register_1_q2),
    .in_6(c39_1_out_11), .in_7(c40_1_out_8), .in_8(c40_1_out_9), .out_9(c44_1_out_9), .out_10(c44_1_out_10));
  not not_3 (nLm, c44_1_out_9);
  not not_4 (nCE, c44_1_out_10);
  Shift_Register #(.length(6)) shift_register_1 (
    .in(nor_1_out), .clk(not_2_out), .clr(CLR), .q0(Ep), .q1(Cp), .q2(shift_register_1_q2),
    .q3(shift_register_1_q3), .q4(shift_register_1_q4), .q5(shift_register_1_q5));  // open: shift, out, load, d0, d1, d2, d3, d4, d5
  C41 c41_1 (
    ._1(controlled_buffer_1_out), ._2(shift_register_1_q3), ._4(decodificador_1_lda),
    ._5(shift_register_1_q4), ._9(decodificador_1_add), ._12(controlled_buffer_1_out),
    ._13(shift_register_1_q5), .out_9(c41_1_out_9), .out_10(c41_1_out_10), .out_11(c41_1_out_11),
    .out_12(c41_1_out_12), .in_1(decodificador_1_cmp));
  C45 c45_1 (
    .in_1(c40_1_out_10), .in_2(c40_1_out_11), .in_3(c41_1_out_9), .in_4(c41_1_out_10), .in_5(c41_1_out_11),
    .in_6(c41_1_out_12), .out_7(c45_1_out_7), .out_8(c45_1_out_8));
  C41 c41_2 (
    ._1(decodificador_1_out), ._2(shift_register_1_q3), ._4(controlled_buffer_1_out),
    ._5(shift_register_1_q5), ._9(decodificador_1_add), ._12(controlled_buffer_1_out),
    ._13(shift_register_1_q5), .out_9(Ea), .out_10(Su), .out_11(c41_2_out_11), .out_12(c41_2_out_12),
    .in_1(decodificador_1_out));
  not not_5 (nLa, c45_1_out_8);
  not not_6 (nEl, c45_1_out_7);
  C46 c46_1 (
    .in_1(c41_2_out_11), .in_2(c41_2_out_12), .in_3(c43_1_out_7), .in_4(c43_1_out_8), .out_5(Eu),
    .out_6(c46_1_out_6));
  C43 c43_1 (
    ._1(decodificador_1_add), .SUB(controlled_buffer_1_out), ._5(shift_register_1_q4),
    ._9(decodificador_1_out), ._10(shift_register_1_q3), .out_7(c43_1_out_7), .out_8(c43_1_out_8),
    .out_9(c43_1_out_9), .in_1(decodificador_1_cmp));
  not not_7 (nLb, c46_1_out_6);
  nor nor_1 (nor_1_out, Ep, Cp, shift_register_1_q2, shift_register_1_q3, shift_register_1_q4);
  not not_8 (nLl, shift_register_1_q2);
  not not_9 (nLo, c43_1_out_9);
  C47 c47_1 (.in_1(shift_register_1_q5), .in_2(decodificador_1_cmp), .out_3(c47_1_out_3));
  not not_10 (Ec, c47_1_out_3);
endmodule

module Decodificador (
  input  l7,
  input  l6,
  input  l5,
  input  l4,
  output LDA,
  output ADD,
  output SUB,
  output CMP,
  output DEC,
  output OUT,
  output HLT
);

  wire and_1_out, and_2_out, and_3_out, and_4_out, and_5_out, and_6_out, and_7_out, not_1_out, not_2_out,
       not_3_out, not_4_out;

  not not_1 (not_1_out, l7);
  not not_2 (not_2_out, l6);
  not not_3 (not_3_out, l5);
  not not_4 (not_4_out, l4);
  buf buffer_1 (LDA, and_1_out);
  and and_1 (and_1_out, not_1_out, not_2_out, not_3_out, not_4_out);
  buf buffer_2 (ADD, and_2_out);
  and and_2 (and_2_out, not_1_out, not_2_out, not_3_out, l4);
  buf buffer_3 (SUB, and_3_out);
  and and_3 (and_3_out, not_1_out, not_2_out, l5, not_4_out);
  and and_4 (and_4_out, not_1_out, l6, not_3_out, not_4_out);
  buf buffer_4 (CMP, and_4_out);
  and and_5 (and_5_out, not_1_out, not_2_out, l5, l4);
  buf buffer_5 (DEC, and_5_out);
  and and_6 (and_6_out, l7, l6, l5, not_4_out);
  buf buffer_6 (OUT, and_6_out);
  and and_7 (and_7_out, l7, l6, l5, l4);
  buf buffer_7 (HLT, and_7_out);
endmodule

module C39 (
  input  in_1,
  input  _9,
  input  _1,
  input  _4,
  input  _10,
  input  _13,
  input  _12,
  output out_8,
  output out_9,
  output out_10,
  output out_11
);

  wire or_1_out;

  and and_1 (out_8, _1, _10);
  or or_1 (or_1_out, in_1, _9);
  and and_2 (out_10, or_1_out, _10);
  and and_3 (out_9, _4, _10);
  and and_4 (out_11, _12, _13);
endmodule

module C40 (
  input  CMP,
  input  SUB,
  input  _1,
  input  _5,
  input  _9,
  input  _12,
  input  _13,
  output out_8,
  output out_9,
  output out_10,
  output out_11
);

  wire or_1_out;

  and and_1 (out_8, _1, _5);
  or or_1 (or_1_out, CMP, SUB);
  and and_2 (out_9, or_1_out, _5);
  and and_3 (out_10, _9, _13);
  and and_4 (out_11, _12, _13);
endmodule

module C41 (
  input  in_1,
  input  _1,
  input  _4,
  input  _5,
  input  _12,
  input  _13,
  input  _2,
  input  _9,
  output out_9,
  output out_10,
  output out_11,
  output out_12
);

  wire or_1_out;

  or or_1 (or_1_out, in_1, _1);
  and and_1 (out_9, or_1_out, _2);
  and and_2 (out_11, _9, _13);
  and and_3 (out_10, _4, _5);
  and and_4 (out_12, _12, _13);
endmodule

module C43 (
  input  in_1,
  input  SUB,
  input  _1,
  input  _5,
  input  _9,
  input  _10,
  output out_7,
  output out_8,
  output out_9
);

  wire or_1_out;

  and and_1 (out_7, _1, _5);
  or or_1 (or_1_out, in_1, SUB);
  and and_2 (out_8, or_1_out, _5);
  and and_3 (out_9, _9, _10);
endmodule

module C44 (
  input  in_1,
  input  in_2,
  input  in_3,
  input  in_4,
  input  in_5,
  input  in_6,
  input  in_7,
  input  in_8,
  output out_9,
  output out_10
);

  or or_1 (out_9, in_1, in_2, in_3, in_4);
  or or_2 (out_10, in_5, in_6, in_7, in_8);
endmodule

module C45 (
  input  in_1,
  input  in_2,
  input  in_3,
  input  in_4,
  input  in_5,
  input  in_6,
  output out_7,
  output out_8
);

  or or_1 (out_7, in_1, in_2, in_3);
  or or_2 (out_8, in_4, in_5, in_6);
endmodule

module C46 (
  input  in_1,
  input  in_2,
  input  in_3,
  input  in_4,
  output out_5,
  output out_6
);

  or or_1 (out_5, in_1, in_2);
  or or_2 (out_6, in_3, in_4);
endmodule

module \Indicação_Visual  (
  input  [7:0] Input,
  input  nLo,
  input  CLK,
  input  CLR,
  output [7:0] Output
);

  wire not_1_out;

  not not_1 (not_1_out, nLo);
  Register register_1 (.D(Input), .en(not_1_out), .Q(Output), .clk(CLK), .clr(CLR));
endmodule

module Comparador (
  input  in_1,
  input  [7:0] A_data,
  input  [7:0] B_data,
  output out_4,
  output out_5
);

  wire not_1_out;
  wire [7:0] controlled_buffer_1_out, controlled_buffer_2_out;

  assign controlled_buffer_1_out = not_1_out ? A_data : 8'bz;  // Controlled_Buffer controlled_buffer_1
  assign controlled_buffer_2_out = not_1_out ? B_data : 8'bz;  // Controlled_Buffer controlled_buffer_2
  Comparator #(.mode("unsigned")) comparator_1 (
    .a(controlled_buffer_1_out), .b(controlled_buffer_2_out), .eq(out_4), .lt(out_5));  // open: gt
  not not_1 (not_1_out, in_1);
endmodule

module C47 (
  input  in_1,
  input  in_2,
  output out_3
);

  and and_1 (out_3, in_1, in_2);
endmodule

module C48 (
  input  in_1,
  input  in_2,
  output out_3
);

  and and_1 (out_3, in_1, in_2);
endmodule
