// Logisim project EP_02_ULA.circ as structural Verilog: 5 circuits, main circuit main
module main (
  input  B3,
  input  B2,
  input  B1,
  input  B0,
  input  A3,
  input  A2,
  input  A1,
  input  A0,
  input  BinVert,
  input  S1,
  input  S0,
  output S0_2,
  output S1_2,
  output S2,
  output S3,
  output Cout
);

  wire ula_1bit_1_cout, ula_1bit_2_cout, ula_1bit_3_cout;

  ULA_1Bit ula_1bit_1 (
    .S(S0_2), .E1(B0), .E0(A0), .Ci(1'b0), .BiVert(BinVert), .Cout(ula_1bit_1_cout), .S1(S1), .S0(S0));
  ULA_1Bit ula_1bit_2 (
    .S(S1_2), .E1(B1), .E0(A1), .Ci(ula_1bit_1_cout), .BiVert(BinVert), .Cout(ula_1bit_2_cout), .S1(S1),
    .S0(S0));
  ULA_1Bit ula_1bit_3 (
    .S(S2), .E1(B2), .E0(A2), .Ci(ula_1bit_2_cout), .BiVert(BinVert), .Cout(ula_1bit_3_cout), .S1(S1), .S0(S0));
  ULA_1Bit ula_1bit_4 (.S(S3), .E1(B3), .E0(A3), .Ci(ula_1bit_3_cout), .BiVert(BinVert), .Cout(Cout), .S1(S1), .S0(S0));
endmodule

module Mux_1S (
  input  A0,
  input  A1,
  input  S0,
  output out_4
);

  wire and_1_out, and_2_out, not_1_out;

  not not_1 (not_1_out, S0);
  and and_1 (and_1_out, S0, A1);
  and and_2 (and_2_out, not_1_out, A0);
  or or_1 (out_4, and_1_out, and_2_out);
endmodule

module Mux_2S (
  input  A3,
  input  A2,
  input  A1,
  input  A0,
  input  S1,
  input  S0,
  output out_7
);

  wire and_1_out, and_2_out, and_3_out, and_4_out, not_1_out, not_2_out, not_3_out, not_4_out;

  and and_1 (and_1_out, A0, not_1_out, not_2_out);
  not not_1 (not_1_out, S1);
  not not_2 (not_2_out, S0);
  and and_2 (and_2_out, A1, not_3_out, S0);
  not not_3 (not_3_out, S1);
  and and_3 (and_3_out, A2, S1, not_4_out);
  not not_4 (not_4_out, S0);
  and and_4 (and_4_out, A3, S1, S0);
  or or_1 (out_7, and_1_out, and_2_out, and_3_out, and_4_out);
endmodule

module ULA_1Bit (
  input  E1,
  input  E0,
  input  S1,
  input  S0,
  input  BiVert,
  input  Ci,
  output S,
  output Cout
);

  wire and_1_out, mux_1s_1_out_4, not_1_out, not_2_out, or_1_out, somador_completo_1_s0;

  not not_1 (not_1_out, E1);
  Mux_1S mux_1s_1 (.out_4(mux_1s_1_out_4), .A0(E1), .A1(not_1_out), .S0(BiVert));
  and and_1 (and_1_out, E0, mux_1s_1_out_4);
  or or_1 (or_1_out, E0, mux_1s_1_out_4);
  not not_2 (not_2_out, E0);
  Somador_Completo somador_completo_1 (.S0(somador_completo_1_s0), .Cout(Cout), .B0(E0), .A0(mux_1s_1_out_4), .Ci(Ci));
  Mux_2S mux_2s_1 (
    .out_7(S), .A3(somador_completo_1_s0), .A2(not_2_out), .A1(or_1_out), .A0(and_1_out), .S1(S1), .S0(S0));
endmodule

// +
module Somador_Completo (
  input  B0,
  input  A0,
  input  Ci,
  output S0,
  output Cout
);

  wire and_1_out, and_2_out, xor_1_out;

  xor xor_1 (xor_1_out, A0, B0);
  and and_1 (and_1_out, A0, B0);
  xor xor_2 (S0, xor_1_out, Ci);
  and and_2 (and_2_out, xor_1_out, Ci);
  or or_1 (Cout, and_2_out, and_1_out);
endmodule
