// Logisim project EP_1.circ as structural Verilog: 5 circuits, main circuit Somador 4Bits
// Sum 4Bits
module Somador_4Bits (
  input  Cin,
  input  A0,
  input  B0,
  input  A1,
  input  B1,
  input  A2,
  input  B2,
  input  A3,
  input  B3,
  output S0,
  output S1,
  output S2,
  output S3,
  output OverFlow,
  output Cout
);

  wire somador_completo_1_cout, somador_completo_2_cout, somador_completo_3_cout;

  Somador_Completo somador_completo_1 (.A0(A0), .B0(B0), .Ci(Cin), .S0(S0), .Cout(somador_completo_1_cout));
  Somador_Completo somador_completo_2 (
    .A0(A1), .B0(B1), .Ci(somador_completo_1_cout), .S0(S1), .Cout(somador_completo_2_cout));
  Somador_Completo somador_completo_3 (
    .A0(A2), .B0(B2), .Ci(somador_completo_2_cout), .S0(S2), .Cout(somador_completo_3_cout));
  Somador_Completo somador_completo_4 (.A0(A3), .B0(B3), .Ci(somador_completo_3_cout), .S0(S3), .Cout(Cout));
  xor xor_1 (OverFlow, somador_completo_3_cout, Cout);
endmodule

module _1_2_Somador (
  input  A,
  input  B,
  output S,
  output Cout
);

  xor xor_1 (S, A, B);
  and and_1 (Cout, A, B);
endmodule

module Somador_Completo (
  input  A0,
  input  B0,
  input  Ci,
  output S0,
  output Cout
);

  wire n1_2_somador_1_cout, n1_2_somador_1_s, n1_2_somador_2_cout;

  _1_2_Somador u_1_2_somador_1 (.A(A0), .B(B0), .S(n1_2_somador_1_s), .Cout(n1_2_somador_1_cout));
  _1_2_Somador u_1_2_somador_2 (.A(n1_2_somador_1_s), .B(Ci), .S(S0), .Cout(n1_2_somador_2_cout));
  or or_1 (Cout, n1_2_somador_2_cout, n1_2_somador_1_cout);
endmodule

module Main (
  input  A0,
  input  A1,
  input  Cin,
  input  A2,
  input  A3,
  input  B0,
  input  B1,
  input  B2,
  input  B3,
  output S3,
  output S2,
  output S1,
  output S0,
  output Cout,
  output OverFlow
);

  wire decodificador_4_p_hex_1_s, decodificador_4_p_hex_1_t, decodificador_4_p_hex_1_u,
       decodificador_4_p_hex_1_v, decodificador_4_p_hex_1_w, decodificador_4_p_hex_1_x,
       decodificador_4_p_hex_1_y, decodificador_4_p_hex_1_z, decodificador_4_p_hex_2_s,
       decodificador_4_p_hex_2_t, decodificador_4_p_hex_2_u, decodificador_4_p_hex_2_v,
       decodificador_4_p_hex_2_w, decodificador_4_p_hex_2_x, decodificador_4_p_hex_2_y,
       decodificador_4_p_hex_2_z, decodificador_4_p_hex_3_s, decodificador_4_p_hex_3_t,
       decodificador_4_p_hex_3_u, decodificador_4_p_hex_3_v, decodificador_4_p_hex_3_w,
       decodificador_4_p_hex_3_x, decodificador_4_p_hex_3_y, decodificador_4_p_hex_3_z;

  Decodificador_4_p__Hex decodificador_4_p_hex_1 (
    .a(A3), .b(A2), .c(A1), .d(A0), .x(decodificador_4_p_hex_1_x), .y(decodificador_4_p_hex_1_y),
    .z(decodificador_4_p_hex_1_z), .u(decodificador_4_p_hex_1_u), .v(decodificador_4_p_hex_1_v),
    .w(decodificador_4_p_hex_1_w), .s(decodificador_4_p_hex_1_s), .t(decodificador_4_p_hex_1_t));
  Decodificador_4_p__Hex decodificador_4_p_hex_2 (
    .a(B3), .b(B2), .c(B1), .d(B0), .x(decodificador_4_p_hex_2_x), .y(decodificador_4_p_hex_2_y),
    .z(decodificador_4_p_hex_2_z), .u(decodificador_4_p_hex_2_u), .v(decodificador_4_p_hex_2_v),
    .w(decodificador_4_p_hex_2_w), .s(decodificador_4_p_hex_2_s), .t(decodificador_4_p_hex_2_t));
  _7_Segment_Display u_7_segment_display_1 (
    .g(decodificador_4_p_hex_1_x), .f(decodificador_4_p_hex_1_y), .a(decodificador_4_p_hex_1_z),
    .b(decodificador_4_p_hex_1_u), .e(decodificador_4_p_hex_1_v), .d(decodificador_4_p_hex_1_w),
    .c(decodificador_4_p_hex_1_s), .dp(decodificador_4_p_hex_1_t));
  Somador_4Bits somador_4bits_1 (
    .A0(A0), .B0(B0), .A1(A1), .B1(B1), .A2(A2), .B2(B2), .A3(A3), .B3(B3), .S0(S0), .S1(S1), .S2(S2),
    .S3(S3), .Cout(Cout), .Cin(Cin), .OverFlow(OverFlow));
  _7_Segment_Display u_7_segment_display_2 (
    .g(decodificador_4_p_hex_2_x), .f(decodificador_4_p_hex_2_y), .a(decodificador_4_p_hex_2_z),
    .b(decodificador_4_p_hex_2_u), .e(decodificador_4_p_hex_2_v), .d(decodificador_4_p_hex_2_w),
    .c(decodificador_4_p_hex_2_s), .dp(decodificador_4_p_hex_2_t));
  Decodificador_4_p__Hex decodificador_4_p_hex_3 (
    .a(S3), .b(S2), .c(S1), .d(S0), .x(decodificador_4_p_hex_3_x), .y(decodificador_4_p_hex_3_y),
    .z(decodificador_4_p_hex_3_z), .u(decodificador_4_p_hex_3_u), .v(decodificador_4_p_hex_3_v),
    .w(decodificador_4_p_hex_3_w), .s(decodificador_4_p_hex_3_s), .t(decodificador_4_p_hex_3_t));
  _7_Segment_Display u_7_segment_display_3 (
    .g(decodificador_4_p_hex_3_x), .f(decodificador_4_p_hex_3_y), .a(decodificador_4_p_hex_3_z),
    .b(decodificador_4_p_hex_3_u), .e(decodificador_4_p_hex_3_v), .d(decodificador_4_p_hex_3_w),
    .c(decodificador_4_p_hex_3_s), .dp(decodificador_4_p_hex_3_t));
endmodule

// Deco 4p8
module Decodificador_4_p__Hex (
  input  a,
  input  b,
  input  c,
  input  d,
  output x,
  output y,
  output z,
  output u,
  output v,
  output w,
  output s,
  output t
);

  wire and_1_out, and_2_out, and_3_out, and_4_out, and_5_out, and_6_out, and_7_out, and_8_out, and_9_out,
       and_10_out, and_11_out, and_12_out, and_13_out, and_14_out, and_15_out, and_16_out, and_17_out,
       and_18_out, and_19_out, and_20_out, and_21_out, and_22_out, and_23_out, and_24_out, and_25_out,
       and_26_out, and_27_out, and_28_out, and_29_out, and_30_out, and_31_out, not_1_out, not_2_out,
       not_3_out, not_4_out, not_5_out, not_6_out, not_7_out, not_8_out, not_9_out, not_10_out, not_11_out,
       not_12_out, not_13_out, not_14_out, not_15_out, not_16_out, not_17_out, not_18_out, not_19_out,
       not_20_out, not_21_out, not_22_out, not_23_out, not_24_out, not_25_out, not_26_out, not_27_out,
       not_28_out, not_29_out, not_30_out, not_31_out, not_32_out, not_33_out, not_34_out, not_35_out,
       not_36_out, not_37_out, not_38_out, not_39_out, not_40_out;

  not not_1 (not_1_out, b);
  and and_1 (and_1_out, not_1_out, c);
  and and_2 (and_2_out, c, not_2_out);
  not not_2 (not_2_out, d);
  not not_3 (not_3_out, a);
  and and_3 (and_3_out, not_3_out, b, not_4_out);
  not not_4 (not_4_out, c);
  and and_4 (and_4_out, a, not_5_out);
  not not_5 (not_5_out, b);
  and and_5 (and_5_out, a, d);
  not not_6 (not_6_out, a);
  and and_6 (and_6_out, not_6_out, not_7_out, not_8_out);
  not not_7 (not_7_out, c);
  not not_8 (not_8_out, d);
  not not_9 (not_9_out, a);
  and and_7 (and_7_out, not_9_out, b);
  and and_8 (and_8_out, a, not_10_out);
  not not_10 (not_10_out, b);
  and and_9 (and_9_out, a, c, not_11_out);
  not not_11 (not_11_out, d);
  not not_12 (not_12_out, b);
  and and_10 (and_10_out, not_12_out, not_13_out);
  not not_13 (not_13_out, d);
  not not_14 (not_14_out, a);
  and and_11 (and_11_out, not_14_out, c);
  not not_15 (not_15_out, a);
  and and_12 (and_12_out, not_15_out, b, d);
  and and_13 (and_13_out, b, c);
  not not_16 (not_16_out, b);
  and and_14 (and_14_out, a, not_16_out, not_17_out);
  not not_17 (not_17_out, c);
  and and_15 (and_15_out, a, not_18_out);
  not not_18 (not_18_out, d);
  not not_19 (not_19_out, a);
  and and_16 (and_16_out, not_19_out, not_20_out);
  not not_20 (not_20_out, b);
  not not_21 (not_21_out, b);
  and and_17 (and_17_out, not_21_out, not_22_out);
  not not_22 (not_22_out, d);
  not not_23 (not_23_out, c);
  and and_18 (and_18_out, not_23_out, not_24_out);
  not not_24 (not_24_out, d);
  and and_19 (and_19_out, b, c, d);
  and and_20 (and_20_out, a, not_25_out);
  not not_25 (not_25_out, c);
  not not_26 (not_26_out, b);
  not not_27 (not_27_out, d);
  not not_28 (not_28_out, d);
  not not_29 (not_29_out, b);
  not not_30 (not_30_out, c);
  not not_31 (not_31_out, a);
  not not_32 (not_32_out, b);
  and and_21 (and_21_out, not_31_out, not_32_out, not_33_out);
  not not_33 (not_33_out, d);
  not not_34 (not_34_out, b);
  and and_22 (and_22_out, not_34_out, c, d);
  and and_23 (and_23_out, b, not_35_out, d);
  not not_35 (not_35_out, c);
  and and_24 (and_24_out, b, c, not_36_out);
  not not_36 (not_36_out, d);
  and and_25 (and_25_out, a, not_37_out);
  not not_37 (not_37_out, c);
  not not_38 (not_38_out, c);
  not not_39 (not_39_out, a);
  and and_26 (and_26_out, not_39_out, b);
  and and_27 (and_27_out, a, not_40_out);
  not not_40 (not_40_out, b);
  or or_1 (x, and_1_out, and_2_out, and_3_out, and_4_out, and_5_out);
  or or_2 (y, and_6_out, and_7_out, and_8_out, and_9_out);
  or or_3 (u, and_16_out, and_17_out, and_18_out, and_19_out, and_20_out);
  and and_28 (and_28_out, not_26_out, not_27_out);
  and and_29 (and_29_out, c, not_28_out);
  and and_30 (and_30_out, a, not_29_out, c);
  and and_31 (and_31_out, a, b, not_30_out, d);
  or or_4 (w, and_21_out, and_22_out, and_23_out, and_24_out, and_25_out);
  or or_5 (s, not_38_out, d, and_26_out, and_27_out);
  or or_6 (z, and_10_out, and_11_out, and_12_out, and_13_out, and_14_out, and_15_out);
  or or_7 (v, and_28_out, and_29_out, and_30_out, and_31_out);

  assign t = 1'b0;
endmodule
